# Fritzing sketch can_update (saved by Fritzing 0.9.10b)

parts:
  M1 = STM32407VG Discovery
  Raspberry_Pi_1 = Raspberry Pi 3 [part_number=RPI-3-V1.2]
  M2 = Niren can bus module [package=THT]
  U1 = MCP2551 [package=so08]
  R1 = Resistor [tolerance=±5% resistance=220 package="0805 [SMD]"]

nets:
  N1: M1.PD1, U1.TXD
  N2: M1.PD0, U1.RXD
  N3: M1.5V-98, U1.VDD
  N4: Raspberry_Pi_1.3v3, M2.pin1
  N5: Raspberry_Pi_1.GIPO10, M2.pin5
  N6: Raspberry_Pi_1.GIPO9, M2.pin4
  N7: Raspberry_Pi_1.GIPO11, M2.pin6
  N8: Raspberry_Pi_1.GIPO12, M2.pin7
  N9: Raspberry_Pi_1.GIPO8, M2.pin3
  N10: Raspberry_Pi_1.GND, M2.pin2
  N11: M2.pin12, U1.CANL
  N12: M2.pin13, U1.CANH
  N13: U1.VSS, R1.Pin_0
  N14: U1.RS, R1.Pin_1

custom parts:
  STM32407VG Discovery: The STM32F4DISCOVERY Discovery kit allows users to easily develop applications with the STM32F407VG high performance microcontroller with the ARM® Cortex®-M4 32-bit core. It includes everything required either for beginners or for experienced users to get quickly started.Based on STM32F407VG, it includes an ST-LINK/V2 or ST-LINK/V2-A embedded debug tool, two ST-MEMS digital accelerometers, a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
  Niren can bus module: Niren can bus module availabe on ebay and others. Pcb view assumes that you unsolder the 7 pin header and resolder it on the bottom of the module to connect to the pcb. The two jumpers and the can bus connector remain on the top of the board and don't appear in pcb view.
