# Fritzing sketch lab4 (saved by Fritzing 0.9.10b)

parts:
  M1 = STM32407VG Discovery
  GY1 = GY-80
  Raspberry_Pi_1 = Raspberry Pi 3 [part_number=RPI-3-V1.2]
  M2 = Niren can bus module [package=THT]
  U1 = MCP2551 [package=so08]
  R1 = Resistor [tolerance=±5% resistance=220 package="0805 [SMD]"]

nets:
  N1: M1.PB11, GY1.SDA
  N2: M1.GND-13, M1.GND-74, GY1.GND
  N3: M1.PB10, GY1.SCL
  N4: M1.PD1, U1.TXD
  N5: M1.3V-72, M1.3V-97, GY1.VCC_3.3V
  N6: M1.PD0, U1.RXD
  N7: M1.5V-98, U1.VDD
  N8: Raspberry_Pi_1.3v3, M2.pin1
  N9: Raspberry_Pi_1.GIPO10, M2.pin5
  N10: Raspberry_Pi_1.GIPO9, M2.pin4
  N11: Raspberry_Pi_1.GIPO11, M2.pin6
  N12: Raspberry_Pi_1.GIPO12, M2.pin7
  N13: Raspberry_Pi_1.GIPO8, M2.pin3
  N14: Raspberry_Pi_1.GND, M2.pin2
  N15: M2.pin12, U1.CANL
  N16: M2.pin13, U1.CANH
  N17: U1.VSS, R1.Pin_0
  N18: U1.RS, R1.Pin_1

custom parts:
  STM32407VG Discovery: The STM32F4DISCOVERY Discovery kit allows users to easily develop applications with the STM32F407VG high performance microcontroller with the ARM® Cortex®-M4 32-bit core. It includes everything required either for beginners or for experienced users to get quickly started.Based on STM32F407VG, it includes an ST-LINK/V2 or ST-LINK/V2-A embedded debug tool, two ST-MEMS digital accelerometers, a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
  GY-80: Placa GY-80 basada en conjunto de giroscopios L3G4200D + acelerómetros ADXL345 + magnetómetro HMC5883L + sensor barométrico BMP085
  Niren can bus module: Niren can bus module availabe on ebay and others. Pcb view assumes that you unsolder the 7 pin header and resolder it on the bottom of the module to connect to the pcb. The two jumpers and the can bus connector remain on the top of the board and don't appear in pcb view.
